# Fritzing sketch zak fritzing (saved by Fritzing 0.9.5d)
breadboards: 1

parts:
  LED1 = LED - 5mm [color="Red (633nm)" package="5 mm [THT]"]
  LED2 = LED - 5mm [color="Yellow (595nm)" package="5 mm [THT]"]
  Part1 = Arduino Uno (Rev3) - ICSP
  S2 = Momentary Switch [package=ksa_sealed_tac_switch]
  S3 = Momentary Switch [package=ksa_sealed_tac_switch]
  R1 = Resistor [tolerance=±5% resistance=1k package="2512 [SMD]"]
  R2 = Resistor [tolerance=±5% resistance=1k package="2512 [SMD]"]
  U1 = SWITCH_SPDT [package=kps-1290]

nets:
  N1: LED1.anode, Part1.D5_PWM
  N2: LED2.anode, Part1.D6_PWM
  N3: Part1.D2, S2.1, R2.Pin_1
  N4: Part1.D3_PWM, U1.P
  N5: Part1.D4, S3.1, R1.Pin_1
  N6: Part1.5V, S2.3, S3.3, U1.O
  N7: Part1.GND, R1.Pin_0, R2.Pin_0, U1.S
